// Digital circuit Alu.dig as structural Verilog
module Alu (
  input  [15:0] x_16,
  input  [15:0] y_16,
  input  zx,
  input  nx,
  input  zy,
  input  ny,
  input  f,
  input  no,
  output [15:0] out_16,
  output zr,
  output ng
);

  wire [15:0] add_1_s, and_1_out, multiplexer_1_out, multiplexer_2_out, multiplexer_5_out, not_1_out,
       not_2_out, not_3_out, Ready_X, Ready_Y;

  Multiplexer #(.Bits(16)) multiplexer_1 (.sel(zx), .in_0(x_16), .in_1({16{1'b0}}), .out(multiplexer_1_out));
  Multiplexer #(.Bits(16)) multiplexer_2 (.sel(zy), .in_0(y_16), .in_1({16{1'b0}}), .out(multiplexer_2_out));
  assign not_1_out = ~multiplexer_1_out;  // Not not_1, 16 bits wide
  assign not_2_out = ~multiplexer_2_out;  // Not not_2, 16 bits wide
  Multiplexer #(.Bits(16)) multiplexer_3 (.sel(nx), .in_0(multiplexer_1_out), .in_1(not_1_out), .out(Ready_X));
  Multiplexer #(.Bits(16)) multiplexer_4 (.sel(ny), .in_0(multiplexer_2_out), .in_1(not_2_out), .out(Ready_Y));
  assign and_1_out = Ready_X & Ready_Y;  // And and_1, 16 bits wide
  Add #(.Bits(16)) add_1 (.a(Ready_X), .b(Ready_Y), .c_i(1'b0), .s(add_1_s));  // open: c_o
  Multiplexer #(.Bits(16)) multiplexer_5 (.sel(f), .in_0(and_1_out), .in_1(add_1_s), .out(multiplexer_5_out));
  assign not_3_out = ~multiplexer_5_out;  // Not not_3, 16 bits wide
  Multiplexer #(.Bits(16)) multiplexer_6 (
    .sel(no), .in_0(multiplexer_5_out), .in_1(not_3_out), .out({ng, out_16[14:0]}));

  assign out_16[15] = ng;

  // Other names for the same wires on the sheet: ReadyOut[15:0] = {ng, out_16[14:0]}
endmodule
