// Digital circuit Bit.dig as structural Verilog
module Bit (
  input  in,
  input  load,
  input  clk,
  output out
);

  wire d_ff_1_q, multiplexer_1_out;

  Multiplexer multiplexer_1 (.sel(load), .in_0(d_ff_1_q), .in_1(in), .out(multiplexer_1_out));
  D_FF d_ff_1 (.D(multiplexer_1_out), .C(clk), .Q(d_ff_1_q), .nQ(out));
endmodule
