// Digital circuit cpu.dig as structural Verilog
module cpu (
  input  [15:0] inM,
  input  [15:0] instruction,
  input  reset
);

  Register register_1 ();  // open: D, C, en, Q
  Register register_2 ();  // open: D, C, en, Q
endmodule
